// Logisim project CirProy2.circ as structural Verilog: 3 circuits, main circuit Octal
module Octal (
  input  in_1,
  input  [63:0] in_2,
  input  [63:0] in_3,
  input  [63:0] in_4,
  input  in_5,
  input  [63:0] in_6,
  input  [63:0] in_7,
  input  in_8,
  input  [63:0] in_9,
  input  [63:0] in_10,
  output [63:0] out_11,
  output [63:0] out_12,
  output out_13,
  output [63:0] out_14,
  output out_15,
  output out_16,
  output [63:0] A_B,
  output [63:0] out_18,
  output out_19,
  output [63:0] out_20,
  output out_21,
  output out_22,
  output [63:0] C_D,
  output out_24
);

  wire undriven, undriven_2;

  Adder #(.width(64)) adder_1 (.a(in_2), .b(in_3), .out(out_11), .cin(in_1), .cout(out_13));
  Adder #(.width(64)) adder_2 (.a(in_6), .b(in_7), .out(A_B), .cin(undriven), .cout(out_19));
  Adder #(.width(64)) adder_3 (.a(in_9), .b(in_10), .out(C_D), .cin(undriven_2), .cout(out_24));
  Subtractor #(.width(64)) subtractor_1 (.a(out_11), .b(in_4), .out(out_12), .bout(out_15));  // open: bin
  Subtractor #(.width(64)) subtractor_2 (.a(A_B), .b(C_D), .out(out_18), .bout(out_21));  // open: bin
  Negator #(.width(64)) negator_1 (.in(out_12), .out(out_14));
  Negator #(.width(64)) negator_2 (.in(out_18), .out(out_20));

  assign out_16 = out_15;
  assign out_22 = out_21;

  // Notes on the sheet:
  //   A
  //   B
  //   C
  //   A
  //   B
  //   C
  //   D
  //   A+B
  //   (A+B)-C POSITIVO
  //   (A+B)-(C+D) POSITIVO
  //   (A+B)-C NEGATIVO
  //   (A+B)-(C+D) NEGATIVO
endmodule

module Hexadecimal (
  input  in_1,
  input  [63:0] in_2,
  input  [63:0] in_3,
  input  [63:0] in_4,
  input  in_5,
  input  [63:0] in_6,
  input  [63:0] in_7,
  input  in_8,
  input  [63:0] in_9,
  input  [63:0] in_10,
  output [63:0] out_11,
  output [63:0] out_12,
  output out_13,
  output [63:0] out_14,
  output out_15,
  output out_16,
  output [63:0] A_B,
  output [63:0] out_18,
  output out_19,
  output [63:0] out_20,
  output out_21,
  output out_22,
  output [63:0] C_D,
  output out_24
);

  wire undriven, undriven_2;

  Adder #(.width(64)) adder_1 (.a(in_2), .b(in_3), .out(out_11), .cin(in_1), .cout(out_13));
  Adder #(.width(64)) adder_2 (.a(in_6), .b(in_7), .out(A_B), .cin(undriven), .cout(out_19));
  Adder #(.width(64)) adder_3 (.a(in_9), .b(in_10), .out(C_D), .cin(undriven_2), .cout(out_24));
  Subtractor #(.width(64)) subtractor_1 (.a(out_11), .b(in_4), .out(out_12), .bout(out_15));  // open: bin
  Subtractor #(.width(64)) subtractor_2 (.a(A_B), .b(C_D), .out(out_18), .bout(out_21));  // open: bin
  Negator #(.width(64)) negator_1 (.in(out_12), .out(out_14));
  Negator #(.width(64)) negator_2 (.in(out_18), .out(out_20));

  assign out_16 = out_15;
  assign out_22 = out_21;

  // Notes on the sheet:
  //   A
  //   B
  //   C
  //   A
  //   B
  //   C
  //   D
  //   A+B
  //   (A+B)-C POSITIVO
  //   (A+B)-(C+D) POSITIVO
  //   (A+B)-C NEGATIVO
  //   (A+B)-(C+D) NEGATIVO
endmodule

module Binario (
  input  in_1,
  input  [7:0] in_2,
  input  [7:0] in_3,
  input  [7:0] in_4,
  input  in_5,
  input  [7:0] in_6,
  input  [7:0] in_7,
  input  in_8,
  input  [7:0] in_9,
  input  [7:0] in_10,
  output [7:0] A_B,
  output [7:0] A_B__C_POSITIVO,
  output out_13,
  output [7:0] A_B__C_NEGATIVO,
  output out_15,
  output out_16,
  output [7:0] A_B_2,
  output [7:0] out_18,
  output out_19,
  output [7:0] out_20,
  output out_21,
  output [7:0] C_D,
  output out_23,
  output out_24
);

  wire undriven, undriven_2, undriven_3;

  Adder adder_1 (.a(in_2), .b(in_3), .out(A_B), .cin(undriven), .cout(out_13));
  Adder adder_2 (.a(in_6), .b(in_7), .out(A_B_2), .cin(undriven_2), .cout(out_19));
  Adder adder_3 (.a(in_9), .b(in_10), .out(C_D), .cin(undriven_3), .cout(out_24));
  Subtractor subtractor_1 (.a(A_B), .b(in_4), .out(A_B__C_POSITIVO), .bout(out_15));  // open: bin
  Subtractor subtractor_2 (.a(A_B_2), .b(C_D), .out(out_18), .bout(out_21));  // open: bin
  Negator negator_1 (.in(A_B__C_POSITIVO), .out(A_B__C_NEGATIVO));
  Negator negator_2 (.in(out_18), .out(out_20));

  assign out_16 = out_15;
  assign out_23 = out_21;

  // Notes on the sheet:
  //   A
  //   B
  //   C
  //   A
  //   B
  //   C
  //   D
  //   (A+B)-(C+D) POSITIVO
  //   (A+B)-(C+D) NEGATIVO
endmodule
