// Logisim project CicuitoY4varTTL.circ as structural Verilog: 1 circuit, main circuit main
module main (
  input  in_1,
  input  in_2,
  input  in_3,
  input  in_4,
  output out_5
);

  wire n7400_1_pin11, n7400_2_pin1, n7400_2_pin3, n7400_2_pin11, n7400_3_pin3, n7400_3_pin6, n7400_3_pin8,
       n7400_3_pin11, n7432_1_pin1, n7432_1_pin3, n7486_1_pin3, n7486_1_pin5, n7486_1_pin6, n7486_1_pin11,
       not_1_out, not_2_out, not_4_out, not_5_out, not_6_out, not_8_out;

  not not_1 (not_1_out, in_2);
  _7400 #(.ShowInternalStructure("true")) u_7400_1 (
    .pin13(in_4), .pin12(in_3), .pin11(n7400_1_pin11));  // open: pin1, pin2, pin3, pin4, pin5, pin6, pin10, pin9, pin8
  not not_2 (not_2_out, n7400_1_pin11);
  _7432 #(.ShowInternalStructure("true")) u_7432_1 (
    .pin1(n7432_1_pin1), .pin2(not_2_out), .pin3(n7432_1_pin3));  // open: pin4, pin5, pin6, pin13, pin12, pin11, pin10, pin9, pin8
  _7400 #(.ShowInternalStructure("true")) u_7400_2 (
    .pin1(n7400_2_pin1), .pin2(in_4), .pin3(n7400_2_pin3), .pin13(in_1), .pin12(not_1_out),
    .pin11(n7400_2_pin11), .pin10(in_2), .pin9(in_1), .pin8(n7432_1_pin1));  // open: pin4, pin5, pin6
  not not_3 (n7400_2_pin1, n7400_2_pin11);
  not not_4 (not_4_out, n7400_2_pin3);
  _7400 #(.ShowInternalStructure("true")) u_7400_3 (
    .pin1(in_3), .pin2(in_4), .pin3(n7400_3_pin3), .pin4(n7400_3_pin3), .pin5(in_2), .pin6(n7400_3_pin6),
    .pin13(in_2), .pin12(in_3), .pin11(n7400_3_pin11), .pin10(n7400_3_pin11), .pin9(in_1), .pin8(n7400_3_pin8));
  not not_5 (not_5_out, n7400_3_pin8);
  not not_6 (not_6_out, n7400_3_pin6);
  _7486 #(.ShowInternalStructure("true")) u_7486_1 (
    .pin1(not_6_out), .pin2(not_5_out), .pin3(n7486_1_pin3), .pin4(n7486_1_pin3), .pin5(n7486_1_pin5),
    .pin6(n7486_1_pin6), .pin13(not_4_out), .pin12(n7432_1_pin3), .pin11(n7486_1_pin11));  // open: pin10, pin9, pin8
  not not_7 (n7486_1_pin5, n7486_1_pin11);
  not not_8 (not_8_out, n7486_1_pin6);
  not not_9 (out_5, not_8_out);
endmodule
