// Logisim project Circ5varTTL.circ as structural Verilog: 1 circuit, main circuit main
module main (
  input  in_1,
  input  in_2,
  input  in_3,
  input  in_4,
  input  in_5,
  output out_6
);

  wire n7400_1_pin3, n7400_1_pin6, n7400_1_pin8, n7400_1_pin10, n7400_1_pin11, n7400_2_pin3, n7400_2_pin4,
       n7400_2_pin6, n7400_2_pin8, n7400_2_pin9, n7400_2_pin11, n7400_3_pin3, n7400_3_pin4, n7400_3_pin6,
       n7400_3_pin8, n7400_3_pin10, n7400_3_pin11, n7400_4_pin3, n7432_1_pin4, n7432_1_pin6, n7432_1_pin11,
       n7432_1_pin13, n7486_1_pin1, n7486_1_pin3, not_5_out, not_8_out, not_9_out, not_11_out;

  _7400 #(.ShowInternalStructure("true")) u_7400_1 (
    .pin1(in_4), .pin2(in_5), .pin3(n7400_1_pin3), .pin4(n7400_1_pin3), .pin5(in_3), .pin6(n7400_1_pin6),
    .pin13(in_1), .pin12(in_2), .pin11(n7400_1_pin11), .pin10(n7400_1_pin10), .pin9(in_3), .pin8(n7400_1_pin8));
  _7400 #(.ShowInternalStructure("true")) u_7400_2 (
    .pin1(in_1), .pin2(in_3), .pin3(n7400_2_pin3), .pin4(n7400_2_pin4), .pin5(in_5), .pin6(n7400_2_pin6),
    .pin13(in_2), .pin12(in_3), .pin11(n7400_2_pin11), .pin10(in_4), .pin9(n7400_2_pin9), .pin8(n7400_2_pin8));
  _7400 #(.ShowInternalStructure("true")) u_7400_3 (
    .pin1(in_2), .pin2(in_5), .pin3(n7400_3_pin3), .pin4(n7400_3_pin4), .pin5(in_3), .pin6(n7400_3_pin6),
    .pin13(in_2), .pin12(in_1), .pin11(n7400_3_pin11), .pin10(n7400_3_pin10), .pin9(in_5), .pin8(n7400_3_pin8));
  not not_1 (n7400_1_pin10, n7400_1_pin11);
  not not_2 (n7400_2_pin4, n7400_2_pin3);
  not not_3 (n7400_3_pin10, n7400_3_pin11);
  not not_4 (n7400_3_pin4, n7400_3_pin3);
  not not_5 (not_5_out, n7400_1_pin8);
  _7432 #(.ShowInternalStructure("true")) u_7432_1 (
    .pin4(n7432_1_pin4), .pin5(n7400_2_pin6), .pin6(n7432_1_pin6), .pin13(n7432_1_pin13), .pin12(not_5_out),
    .pin11(n7432_1_pin11));  // open: pin1, pin2, pin3, pin10, pin9, pin8
  not not_6 (n7432_1_pin13, n7400_1_pin6);
  not not_7 (n7400_2_pin9, n7400_2_pin11);
  not not_8 (not_8_out, n7400_3_pin6);
  not not_9 (not_9_out, n7432_1_pin11);
  not not_10 (n7432_1_pin4, n7400_2_pin8);
  not not_11 (not_11_out, n7400_3_pin8);
  _7400 #(.ShowInternalStructure("true")) u_7400_4 (
    .pin1(not_11_out), .pin2(not_8_out), .pin3(n7400_4_pin3));  // open: pin4, pin5, pin6, pin13, pin12, pin11, pin10, pin9, pin8
  _7486 #(.ShowInternalStructure("true")) u_7486_1 (
    .pin1(n7486_1_pin1), .pin2(n7400_4_pin3), .pin3(n7486_1_pin3), .pin13(n7432_1_pin6), .pin12(not_9_out),
    .pin11(n7486_1_pin1));  // open: pin4, pin5, pin6, pin10, pin9, pin8
  not not_12 (out_6, n7486_1_pin3);
endmodule
