// Logisim project CircW5varCom.circ as structural Verilog: 1 circuit, main circuit main
module main (
  input  in_1,
  input  in_2,
  input  in_3,
  input  in_4,
  input  in_5,
  input  AW,
  input  BW,
  input  CW,
  input  DW,
  input  EW,
  output out_11,
  output out_12
);

  wire and_1_out, and_2_out, and_3_out, and_4_out, and_5_out, and_6_out, and_7_out, and_8_out, and_9_out,
       and_10_out, and_11_out, and_12_out, and_13_out, and_14_out, and_15_out, and_16_out, and_17_out,
       nand_1_out, nor_1_out, not_1_out, not_2_out, not_3_out, not_4_out, not_5_out, not_6_out, not_7_out,
       not_8_out, not_9_out, not_10_out, not_11_out, or_1_out, or_2_out, or_3_out, or_4_out, or_5_out,
       or_6_out, xor_1_out;

  and and_1 (and_1_out, AW, BW);
  and and_2 (and_2_out, CW, and_6_out);
  and and_3 (and_3_out, AW, CW);
  and and_4 (and_4_out, BW, EW);
  and and_5 (and_5_out, and_1_out, CW);
  not not_1 (not_1_out, and_2_out);
  and and_6 (and_6_out, DW, EW);
  and and_7 (and_7_out, CW, BW);
  and and_8 (and_8_out, and_3_out, EW);
  and and_9 (and_9_out, AW, BW);
  and and_10 (and_10_out, and_7_out, DW);
  not not_2 (not_2_out, and_8_out);
  and and_11 (and_11_out, and_4_out, CW);
  nor nor_1 (nor_1_out, and_5_out, not_1_out);
  and and_12 (and_12_out, and_9_out, DW);
  not not_3 (not_3_out, and_11_out);
  or or_1 (or_1_out, and_10_out, not_2_out);
  nand nand_1 (nand_1_out, and_12_out, not_3_out);
  xor xor_1 (xor_1_out, nor_1_out, or_1_out);
  xnor xnor_1 (out_12, xor_1_out, nand_1_out);
  not not_4 (not_4_out, in_5);
  not not_5 (not_5_out, in_4);
  not not_6 (not_6_out, in_3);
  not not_7 (not_7_out, in_1);
  not not_8 (not_8_out, in_3);
  not not_9 (not_9_out, in_5);
  not not_10 (not_10_out, in_2);
  or or_2 (or_2_out, not_4_out, not_5_out);
  not not_11 (not_11_out, in_4);
  or or_3 (or_3_out, not_8_out, not_9_out);
  and and_13 (and_13_out, in_1, in_4);
  and and_14 (and_14_out, in_3, in_5);
  or or_4 (or_4_out, or_2_out, not_6_out);
  and and_15 (and_15_out, not_11_out, or_3_out);
  or or_5 (or_5_out, not_10_out, and_14_out);
  and and_16 (and_16_out, or_4_out, not_7_out);
  or or_6 (or_6_out, and_16_out, and_15_out);
  and and_17 (and_17_out, and_13_out, or_5_out);
  or or_7 (out_11, or_6_out, and_17_out);
endmodule
