// Logisim project CircW5varTTL.circ as structural Verilog: 1 circuit, main circuit main
module main (
  input  in_1,
  input  in_2,
  input  in_3,
  input  in_4,
  input  in_5,
  input  AW,
  input  BW,
  input  CW,
  input  DW,
  input  EW,
  output out_11,
  output out_12
);

  wire n7400_1_pin3, n7400_1_pin4, n7400_1_pin6, n7400_1_pin8, n7400_1_pin11, n7400_2_pin3, n7400_2_pin4,
       n7400_2_pin6, n7400_2_pin8, n7400_2_pin9, n7400_2_pin11, n7400_3_pin3, n7400_3_pin4, n7400_3_pin6,
       n7400_3_pin8, n7400_3_pin11, n7400_4_pin3, n7400_5_pin3, n7400_5_pin6, n7400_5_pin8, n7400_5_pin11,
       n7400_6_pin3, n7432_1_pin4, n7432_1_pin6, n7432_1_pin11, n7432_2_pin3, n7432_2_pin8, n7432_2_pin11,
       n7432_3_pin4, n7432_3_pin5, n7432_3_pin9, n7432_3_pin10, n7432_3_pin11, n7486_1_pin1, n7486_1_pin3,
       not_1_out, not_4_out, not_7_out, not_9_out, not_10_out, not_12_out, not_13_out, not_14_out,
       not_15_out, not_16_out, not_17_out, not_18_out, not_19_out, not_20_out, not_22_out;

  not not_1 (not_1_out, n7400_1_pin11);
  _7400 #(.ShowInternalStructure("true")) u_7400_1 (
    .pin1(DW), .pin2(EW), .pin3(n7400_1_pin3), .pin4(n7400_1_pin4), .pin5(CW), .pin6(n7400_1_pin6),
    .pin13(AW), .pin12(BW), .pin11(n7400_1_pin11), .pin10(not_1_out), .pin9(CW), .pin8(n7400_1_pin8));
  not not_2 (n7400_1_pin4, n7400_1_pin3);
  _7400 #(.ShowInternalStructure("true")) u_7400_2 (
    .pin1(AW), .pin2(CW), .pin3(n7400_2_pin3), .pin4(n7400_2_pin4), .pin5(EW), .pin6(n7400_2_pin6),
    .pin13(BW), .pin12(CW), .pin11(n7400_2_pin11), .pin10(DW), .pin9(n7400_2_pin9), .pin8(n7400_2_pin8));
  not not_3 (n7400_2_pin4, n7400_2_pin3);
  not not_4 (not_4_out, n7400_3_pin11);
  _7400 #(.ShowInternalStructure("true")) u_7400_3 (
    .pin1(BW), .pin2(EW), .pin3(n7400_3_pin3), .pin4(n7400_3_pin4), .pin5(CW), .pin6(n7400_3_pin6),
    .pin13(BW), .pin12(AW), .pin11(n7400_3_pin11), .pin10(not_4_out), .pin9(DW), .pin8(n7400_3_pin8));
  not not_5 (n7400_3_pin4, n7400_3_pin3);
  not not_6 (n7400_2_pin9, n7400_2_pin11);
  not not_7 (not_7_out, n7400_1_pin8);
  _7432 #(.ShowInternalStructure("true")) u_7432_1 (
    .pin4(n7432_1_pin4), .pin5(n7400_2_pin6), .pin6(n7432_1_pin6), .pin13(n7400_1_pin6), .pin12(not_7_out),
    .pin11(n7432_1_pin11));  // open: pin1, pin2, pin3, pin10, pin9, pin8
  not not_8 (n7432_1_pin4, n7400_2_pin8);
  not not_9 (not_9_out, n7400_3_pin8);
  not not_10 (not_10_out, n7432_1_pin11);
  _7400 #(.ShowInternalStructure("true")) u_7400_4 (
    .pin1(not_9_out), .pin2(n7400_3_pin6), .pin3(n7400_4_pin3));  // open: pin4, pin5, pin6, pin13, pin12, pin11, pin10, pin9, pin8
  _7486 #(.ShowInternalStructure("true")) u_7486_1 (
    .pin1(n7486_1_pin1), .pin2(n7400_4_pin3), .pin3(n7486_1_pin3), .pin13(n7432_1_pin6), .pin12(not_10_out),
    .pin11(n7486_1_pin1));  // open: pin4, pin5, pin6, pin10, pin9, pin8
  not not_11 (out_12, n7486_1_pin3);
  not not_12 (not_12_out, in_1);
  not not_13 (not_13_out, in_3);
  not not_14 (not_14_out, in_4);
  not not_15 (not_15_out, in_5);
  not not_16 (not_16_out, in_3);
  not not_17 (not_17_out, in_2);
  not not_18 (not_18_out, in_5);
  _7432 #(.ShowInternalStructure("true")) u_7432_2 (
    .pin1(not_16_out), .pin2(not_15_out), .pin3(n7432_2_pin3), .pin13(not_13_out), .pin12(not_14_out),
    .pin11(n7432_2_pin11), .pin10(not_18_out), .pin9(n7432_2_pin11), .pin8(n7432_2_pin8));  // open: pin4, pin5, pin6
  not not_19 (not_19_out, in_4);
  _7400 #(.ShowInternalStructure("true")) u_7400_5 (
    .pin1(in_5), .pin2(in_3), .pin3(n7400_5_pin3), .pin4(in_1), .pin5(in_4), .pin6(n7400_5_pin6),
    .pin13(n7432_2_pin3), .pin12(not_19_out), .pin11(n7400_5_pin11), .pin10(n7432_2_pin8), .pin9(not_12_out),
    .pin8(n7400_5_pin8));
  not not_20 (not_20_out, n7400_5_pin3);
  _7432 #(.ShowInternalStructure("true")) u_7432_3 (
    .pin4(n7432_3_pin4), .pin5(n7432_3_pin5), .pin6(out_11), .pin13(not_20_out), .pin12(not_17_out),
    .pin11(n7432_3_pin11), .pin10(n7432_3_pin10), .pin9(n7432_3_pin9), .pin8(n7432_3_pin4));  // open: pin1, pin2, pin3
  not not_21 (n7432_3_pin10, n7400_5_pin11);
  not not_22 (not_22_out, n7400_5_pin6);
  not not_23 (n7432_3_pin5, n7400_5_pin8);
  _7400 #(.ShowInternalStructure("true")) u_7400_6 (
    .pin1(n7432_3_pin11), .pin2(not_22_out), .pin3(n7400_6_pin3));  // open: pin4, pin5, pin6, pin13, pin12, pin11, pin10, pin9, pin8
  not not_24 (n7432_3_pin9, n7400_6_pin3);

  // Notes on the sheet:
  //   W en TTL original y simplificada 
endmodule
