// Logisim project CircX3var.circ as structural Verilog: 1 circuit, main circuit main
module main (
  input  A,
  input  in_2,
  input  B,
  input  C,
  input  in_5,
  input  in_6,
  output out_7,
  output out_8
);

  wire and_1_out, and_2_out, and_3_out, and_4_out, dipswitch_1_p1, dipswitch_1_p2, dipswitch_1_p3,
       dipswitch_2_p3, n7404_1_pin2, n7404_1_pin3, n7404_1_pin4, n7404_1_pin6, n7404_2_pin1, n7404_2_pin2,
       n7404_2_pin3, n7404_2_pin4, n7408_1_pin11, n7408_2_pin2, n7408_2_pin3, n7408_2_pin6, n7408_2_pin8,
       n7408_2_pin11, n7408_2_pin12, n7432_1_pin8, n7432_2_pin8, n7432_2_pin11, n7486_1_pin11, not_1_out,
       not_2_out, not_4_out, not_5_out, or_1_out, or_2_out, xnor_1_out, xor_1_out;

  // DipSwitch #(.number(3)) dipswitch_1: pin names not known; wires that end beside it: dipswitch_1_p1, dipswitch_1_p2, dipswitch_1_p3
  _7408 #(.ShowInternalStructure("true")) u_7408_1 (
    .pin13(dipswitch_1_p3), .pin12(dipswitch_1_p2), .pin11(n7408_1_pin11));  // open: pin1, pin2, pin3, pin4, pin5, pin6, pin10, pin9, pin8
  not not_1 (not_1_out, B);
  or or_1 (or_1_out, A, B);
  and and_1 (and_1_out, A, not_1_out, C);
  and and_2 (and_2_out, A, B);
  and and_3 (and_3_out, C, B);
  _7408 #(.ShowInternalStructure("true")) u_7408_2 (
    .pin1(dipswitch_1_p3), .pin2(n7408_2_pin2), .pin3(n7408_2_pin3), .pin4(dipswitch_1_p1),
    .pin5(dipswitch_1_p2), .pin6(n7408_2_pin6), .pin13(dipswitch_1_p1), .pin12(n7408_2_pin12),
    .pin11(n7408_2_pin11), .pin10(n7408_2_pin11), .pin9(dipswitch_1_p3), .pin8(n7408_2_pin8));
  _7432 #(.ShowInternalStructure("true")) u_7432_1 (
    .pin13(dipswitch_1_p1), .pin12(dipswitch_1_p2), .pin11(n7408_2_pin2), .pin10(n7408_2_pin6),
    .pin9(n7408_1_pin11), .pin8(n7432_1_pin8));  // open: pin1, pin2, pin3, pin4, pin5, pin6
  and and_4 (and_4_out, or_1_out, C);
  or or_2 (or_2_out, and_2_out, and_3_out);
  not not_2 (not_2_out, or_2_out);
  xor xor_1 (xor_1_out, and_4_out, and_1_out);
  xnor xnor_1 (xnor_1_out, xor_1_out, not_2_out);
  _7404 #(.ShowInternalStructure("true")) u_7404_1 (
    .pin1(n7432_1_pin8), .pin2(n7404_1_pin2), .pin3(n7404_1_pin3), .pin4(n7404_1_pin4), .pin5(n7404_1_pin4),
    .pin6(n7404_1_pin6), .pin13(dipswitch_1_p2), .pin12(n7408_2_pin12));  // open: pin11, pin10, pin9, pin8
  _7486 #(.ShowInternalStructure("true")) u_7486_1 (
    .pin13(n7408_2_pin3), .pin12(n7408_2_pin8), .pin11(n7486_1_pin11), .pin10(n7486_1_pin11),
    .pin9(n7404_1_pin2), .pin8(n7404_1_pin3));  // open: pin1, pin2, pin3, pin4, pin5, pin6
  not not_3 (out_8, xnor_1_out);
  // Probe on n7404_1_pin6
  _7404 #(.ShowInternalStructure("true")) u_7404_2 (
    .pin1(n7404_2_pin1), .pin2(n7404_2_pin2), .pin3(n7404_2_pin3), .pin4(n7404_2_pin4));  // open: pin5, pin6, pin13, pin12, pin11, pin10, pin9, pin8
  // DipSwitch #(.number(3)) dipswitch_2: pin names not known; wires that end beside it: n7404_2_pin1, n7404_2_pin3, dipswitch_2_p3
  _7432 #(.ShowInternalStructure("true")) u_7432_2 (
    .pin13(n7404_2_pin2), .pin12(n7404_2_pin4), .pin11(n7432_2_pin11), .pin10(n7432_2_pin11),
    .pin9(dipswitch_2_p3), .pin8(n7432_2_pin8));  // open: pin1, pin2, pin3, pin4, pin5, pin6
  not not_4 (not_4_out, in_2);
  not not_5 (not_5_out, in_5);
  // Probe on n7432_2_pin8
  or or_3 (out_7, not_4_out, not_5_out, in_6);

  // Notes on the sheet:
  //   X ORIGINAL
  //   X TTL ORIGINAL 
  //   X SIMPLIFICADA
  //   X SIMPLIFICADA TTL
endmodule
