// Logisim project CircY4var.circ as structural Verilog: 1 circuit, main circuit main
module main (
  input  in_1,
  input  in_2,
  input  in_3,
  input  in_4,
  input  in_5,
  input  in_6,
  input  in_7,
  input  in_8,
  output out_9,
  output out_10
);

  wire and_1_out, and_2_out, and_3_out, and_4_out, and_5_out, and_6_out, and_7_out, and_8_out, and_9_out,
       and_10_out, and_11_out, dipswitch_1_p1, dipswitch_1_p2, dipswitch_1_p3, dipswitch_1_p4, n7404_1_pin3,
       n7404_1_pin4, n7404_1_pin12, n7408_1_pin3, n7408_1_pin6, n7408_1_pin8, n7408_1_pin11, n7408_1_pin12,
       n7408_2_pin6, n7408_2_pin8, n7408_2_pin10, n7408_2_pin11, n7432_1_pin3, n7486_1_pin3, n7486_1_pin4,
       n7486_1_pin5, n7486_1_pin6, not_1_out, not_2_out, not_3_out, not_4_out, not_6_out, not_7_out,
       not_8_out, not_9_out, not_10_out, not_11_out, not_12_out, not_13_out, or_1_out, or_2_out, or_3_out,
       xnor_1_out, xnor_2_out, xor_1_out;

  // DipSwitch #(.number(4)) dipswitch_1: pin names not known; wires that end beside it: dipswitch_1_p1, dipswitch_1_p2, dipswitch_1_p3, dipswitch_1_p4
  and and_1 (and_1_out, in_1, in_3);
  and and_2 (and_2_out, in_5, in_7);
  not not_1 (not_1_out, in_3);
  and and_3 (and_3_out, in_3, in_5);
  and and_4 (and_4_out, in_5, in_7);
  _7408 #(.ShowInternalStructure("true")) u_7408_1 (
    .pin1(dipswitch_1_p1), .pin2(dipswitch_1_p2), .pin3(n7408_1_pin3), .pin4(dipswitch_1_p3),
    .pin5(dipswitch_1_p4), .pin6(n7408_1_pin6), .pin13(dipswitch_1_p1), .pin12(n7408_1_pin12),
    .pin11(n7408_1_pin11), .pin10(n7408_1_pin11), .pin9(dipswitch_1_p4), .pin8(n7408_1_pin8));
  _7404 #(.ShowInternalStructure("true")) u_7404_1 (
    .pin1(dipswitch_1_p2), .pin2(n7408_1_pin12), .pin3(n7404_1_pin3), .pin4(n7404_1_pin4),
    .pin13(n7408_1_pin3), .pin12(n7404_1_pin12));  // open: pin5, pin6, pin11, pin10, pin9, pin8
  not not_2 (not_2_out, and_1_out);
  and and_5 (and_5_out, in_1, not_1_out, in_7);
  and and_6 (and_6_out, in_1, not_3_out);
  not not_3 (not_3_out, and_3_out);
  and and_7 (and_7_out, in_3, not_4_out);
  not not_4 (not_4_out, and_4_out);
  or or_1 (or_1_out, not_2_out, and_2_out);
  xor xor_1 (xor_1_out, and_6_out, and_7_out);
  _7432 #(.ShowInternalStructure("true")) u_7432_1 (
    .pin1(n7404_1_pin12), .pin2(n7408_1_pin6), .pin3(n7432_1_pin3));  // open: pin4, pin5, pin6, pin13, pin12, pin11, pin10, pin9, pin8
  _7408 #(.ShowInternalStructure("true")) u_7408_2 (
    .pin1(dipswitch_1_p2), .pin2(dipswitch_1_p3), .pin3(n7404_1_pin3), .pin4(n7404_1_pin4),
    .pin5(dipswitch_1_p1), .pin6(n7408_2_pin6), .pin13(dipswitch_1_p3), .pin12(dipswitch_1_p4),
    .pin11(n7408_2_pin11), .pin10(n7408_2_pin10), .pin9(dipswitch_1_p3), .pin8(n7408_2_pin8));
  xnor xnor_1 (xnor_1_out, or_1_out, and_5_out);
  xnor xnor_2 (xnor_2_out, xnor_1_out, xor_1_out);
  not not_5 (out_9, xnor_2_out);
  _7486 #(.ShowInternalStructure("true")) u_7486_1 (
    .pin1(n7432_1_pin3), .pin2(n7408_1_pin8), .pin3(n7486_1_pin3), .pin4(n7486_1_pin4), .pin5(n7486_1_pin5),
    .pin6(n7486_1_pin6), .pin13(n7408_2_pin6), .pin12(n7408_2_pin8), .pin11(n7486_1_pin5));  // open: pin10, pin9, pin8
  _7404 #(.ShowInternalStructure("true")) u_7404_2 (
    .pin13(n7486_1_pin3), .pin12(n7486_1_pin4), .pin11(n7408_2_pin11), .pin10(n7408_2_pin10));  // open: pin1, pin2, pin3, pin4, pin5, pin6, pin9, pin8
  // Probe on n7486_1_pin6
  not not_6 (not_6_out, in_2);
  not not_7 (not_7_out, in_6);
  not not_8 (not_8_out, in_4);
  not not_9 (not_9_out, in_6);
  not not_10 (not_10_out, in_4);
  not not_11 (not_11_out, in_8);
  not not_12 (not_12_out, in_2);
  not not_13 (not_13_out, in_8);
  and and_8 (and_8_out, not_6_out, in_4, not_7_out);
  and and_9 (and_9_out, not_12_out, in_4, not_13_out);
  and and_10 (and_10_out, in_2, not_8_out, not_9_out, in_8);
  and and_11 (and_11_out, in_2, not_10_out, in_6, not_11_out);
  or or_2 (or_2_out, and_8_out, and_9_out);
  or or_3 (or_3_out, or_2_out, and_10_out);
  or or_4 (out_10, or_3_out, and_11_out);
endmodule
