// Logisim project CircY4varSTTL.circ as structural Verilog: 1 circuit, main circuit main
module main (
  input  in_1,
  input  in_2,
  input  in_3,
  input  in_4,
  output out_5
);

  wire n7400_1_pin2, n7400_1_pin3, n7400_1_pin8, n7400_1_pin9, n7400_1_pin10, n7432_1_pin4, n7432_1_pin5;

  _7400 #(.ShowInternalStructure("true")) u_7400_1 (
    .pin1(in_2), .pin2(n7400_1_pin2), .pin3(n7400_1_pin3), .pin10(n7400_1_pin10), .pin9(n7400_1_pin9),
    .pin8(n7400_1_pin8));  // open: pin4, pin5, pin6, pin13, pin12, pin11
  not not_1 (n7400_1_pin2, in_3);
  not not_2 (n7400_1_pin10, in_4);
  _7432 #(.ShowInternalStructure("true")) u_7432_1 (
    .pin1(in_1), .pin2(in_2), .pin3(n7400_1_pin9), .pin4(n7432_1_pin4), .pin5(n7432_1_pin5), .pin6(out_5));  // open: pin13, pin12, pin11, pin10, pin9, pin8
  not not_3 (n7432_1_pin4, n7400_1_pin3);
  not not_4 (n7432_1_pin5, n7400_1_pin8);
endmodule
