// Logisim project CircZ3var.circ as structural Verilog: 1 circuit, main circuit main
module main (
  input  A,
  input  B,
  input  C,
  input  in_4,
  input  in_5,
  output out_6,
  output out_7,
  output out_8,
  output out_9,
  output out_10,
  output out_11,
  output out_12,
  output out_13,
  output out_14,
  output out_15
);

  wire and_1_out, dipswitch_1_sw1, dipswitch_1_sw2, dipswitch_1_sw3, dipswitch_2_sw1, dipswitch_2_sw2,
       n7404_1_pin1, n7404_1_pin2, n7404_1_pin5, n7404_1_pin6, n7404_1_pin12, n7408_1_pin3, n7408_1_pin8,
       n7408_1_pin11, n7432_1_pin4, n7432_1_pin5, n7432_1_pin6, n7432_1_pin11, n7432_2_pin11;

  DipSwitch #(.number(3)) dipswitch_1 (.sw1(dipswitch_1_sw1), .sw2(dipswitch_1_sw2), .sw3(dipswitch_1_sw3));
  not not_1 (out_12, A);
  _7408 #(.ShowInternalStructure("true")) u_7408_1 (
    .pin1(dipswitch_1_sw2), .pin2(dipswitch_1_sw3), .pin3(n7408_1_pin3), .pin13(dipswitch_1_sw1),
    .pin12(dipswitch_1_sw2), .pin11(n7408_1_pin11), .pin10(n7408_1_pin11), .pin9(dipswitch_1_sw3),
    .pin8(n7408_1_pin8));  // open: pin4, pin5, pin6
  _7432 #(.ShowInternalStructure("true")) u_7432_1 (
    .pin4(n7432_1_pin4), .pin5(n7432_1_pin5), .pin6(n7432_1_pin6), .pin13(dipswitch_1_sw1),
    .pin12(dipswitch_1_sw2), .pin11(n7432_1_pin11));  // open: pin1, pin2, pin3, pin10, pin9, pin8
  and and_1 (and_1_out, A, B, C);
  or or_1 (out_9, A, B);
  and and_2 (out_14, B, C);
  not not_2 (out_6, and_1_out);
  not not_3 (out_15, out_14);
  or or_2 (out_13, out_12, out_15);
  _7404 #(.ShowInternalStructure("true")) u_7404_1 (
    .pin1(n7404_1_pin1), .pin2(n7404_1_pin2), .pin3(n7408_1_pin3), .pin4(n7432_1_pin5), .pin5(n7404_1_pin5),
    .pin6(n7404_1_pin6), .pin13(n7408_1_pin8), .pin12(n7404_1_pin12), .pin11(dipswitch_1_sw1),
    .pin10(n7432_1_pin4));  // open: pin9, pin8
  _7486 #(.ShowInternalStructure("true")) u_7486_1 (
    .pin13(n7404_1_pin12), .pin12(n7432_1_pin11), .pin11(n7404_1_pin1), .pin10(n7404_1_pin2),
    .pin9(n7432_1_pin6), .pin8(n7404_1_pin5));  // open: pin1, pin2, pin3, pin4, pin5, pin6
  xnor xnor_1 (out_7, out_6, out_9);
  xor xor_1 (out_8, out_7, out_13);
  not not_4 (out_10, out_8);
  // Probe on n7404_1_pin6
  DipSwitch #(.number(2)) dipswitch_2 (.sw1(dipswitch_2_sw1), .sw2(dipswitch_2_sw2));
  _7432 #(.ShowInternalStructure("true")) u_7432_2 (
    .pin13(dipswitch_2_sw1), .pin12(dipswitch_2_sw2), .pin11(n7432_2_pin11));  // open: pin1, pin2, pin3, pin4, pin5, pin6, pin10, pin9, pin8
  or or_3 (out_11, in_4, in_5);
  // Probe on n7432_2_pin11

  // Notes on the sheet:
  //   Z version original
  //   Z version simplificada
endmodule
