// Logisim project DECB.circ as structural Verilog: 1 circuit, main circuit main
module main (
  input  in_1,
  input  in_2,
  input  in_3,
  input  in_4,
  input  in_5,
  input  in_6,
  input  in_7,
  input  in_8,
  input  in_9,
  input  in_10,
  input  in_11,
  input  in_12,
  output out_13,
  output out_14,
  output out_15,
  output out_16,
  output out_17,
  output out_18,
  output out_19,
  output out_20,
  output out_21,
  output out_22,
  output out_23,
  output out_24,
  output out_25,
  output out_26,
  output out_27,
  output out_28,
  output out_29,
  output out_30,
  output out_31,
  output out_32,
  output out_33,
  output out_34,
  output out_35,
  output out_36,
  output out_37,
  output out_38,
  output out_39,
  output out_40,
  output out_41,
  output out_42,
  output out_43,
  output out_44,
  output out_45,
  output out_46,
  output out_47,
  output out_48,
  output out_49,
  output out_50,
  output out_51,
  output out_52,
  output out_53,
  output out_54,
  output out_55,
  output out_56,
  output out_57,
  output out_58,
  output out_59,
  output out_60,
  output out_61,
  output out_62,
  output out_63,
  output out_64,
  output out_65,
  output out_66,
  output out_67,
  output out_68,
  output out_69,
  output out_70,
  output out_71,
  output out_72,
  output out_73,
  output out_74,
  output out_75,
  output out_76,
  output out_77,
  output out_78,
  output out_79,
  output out_80,
  output out_81,
  output out_82,
  output out_83,
  output out_84,
  output out_85,
  output out_86,
  output out_87,
  output out_88,
  output out_89,
  output out_90,
  output out_91,
  output out_92,
  output out_93,
  output out_94,
  output out_95,
  output out_96,
  output out_97,
  output out_98,
  output out_99,
  output out_100,
  output out_101,
  output out_102,
  output out_103,
  output out_104,
  output out_105,
  output out_106,
  output out_107,
  output out_108
);

  wire not_1_out;

  Decoder #(.select(5)) decoder_1 (
    .out0(out_14), .out1(out_16), .out2(out_18), .out3(out_20), .out4(out_22), .out5(out_24), .out6(out_26),
    .out7(out_28), .out8(out_30), .out9(out_32), .out10(out_34), .out11(out_36), .out12(out_38),
    .out13(out_40), .out14(out_42), .out15(out_44), .out16(out_46), .out17(out_48), .out18(out_50),
    .out19(out_52), .out20(out_54), .out21(out_56), .out22(out_58), .out23(out_60), .out24(out_62),
    .out25(out_64), .out26(out_66), .out27(out_68), .out28(out_70), .out29(out_72), .out30(out_74),
    .out31(out_76), .sel({in_8, in_9, in_10, in_11, in_12}), .en(in_7));
  Decoder #(.select(5)) decoder_2 (
    .out0(out_13), .out1(out_15), .out2(out_17), .out3(out_19), .out4(out_21), .out5(out_23), .out6(out_25),
    .out7(out_27), .out8(out_29), .out9(out_31), .out10(out_33), .out11(out_35), .out12(out_37),
    .out13(out_39), .out14(out_41), .out15(out_43), .out16(out_45), .out17(out_47), .out18(out_49),
    .out19(out_51), .out20(out_53), .out21(out_55), .out22(out_57), .out23(out_59), .out24(out_61),
    .out25(out_63), .out26(out_65), .out27(out_67), .out28(out_69), .out29(out_71), .out30(out_73),
    .out31(out_75), .sel({in_2, in_3, in_4, in_5, in_6}), .en(not_1_out));
  not not_1 (not_1_out, in_1);
  Decoder #(.select(5)) decoder_3 (
    .out0(out_77), .out1(out_78), .out2(out_79), .out3(out_80), .out4(out_81), .out5(out_82), .out6(out_83),
    .out7(out_84), .out8(out_85), .out9(out_86), .out10(out_87), .out11(out_88), .out12(out_89),
    .out13(out_90), .out14(out_91), .out15(out_92), .out16(out_93), .out17(out_94), .out18(out_95),
    .out19(out_96), .out20(out_97), .out21(out_98), .out22(out_99), .out23(out_100), .out24(out_101),
    .out25(out_102), .out26(out_103), .out27(out_104), .out28(out_105), .out29(out_106), .out30(out_107),
    .out31(out_108), .sel({in_2, in_3, in_4, in_5, in_6}), .en(in_1));
endmodule
