// Logisim project Demuxa.circ as structural Verilog: 2 circuits, main circuit main
module main (
  input  [63:0] in_1,
  input  in_2,
  input  in_3,
  input  in_4,
  input  in_5,
  input  in_6
);

  Demultiplexer #(.select(5), .width(64)) demultiplexer_1 (
    .in(in_1), .sel({in_2, in_4, in_3, in_6, in_5}));  // open: out0, out1, out2, out3, out4, out5, out6, out7, out8, out9, out10, out11, out12, out13, out14, out15, out16, out17, out18, out19, out20, out21, out22, out23, out24, out25, out26, out27, out28, out29, out30, out31
endmodule

module demuxa (
  input  in_1,
  input  in_2,
  input  in_3,
  input  in_4,
  input  in_5,
  input  in_6,
  output out_7,
  output out_8,
  output out_9,
  output out_10,
  output out_11,
  output out_12,
  output out_13,
  output out_14,
  output out_15,
  output out_16,
  output out_17,
  output out_18,
  output out_19,
  output out_20,
  output out_21,
  output out_22,
  output out_23,
  output out_24,
  output out_25,
  output out_26,
  output out_27,
  output out_28,
  output out_29,
  output out_30,
  output out_31,
  output out_32,
  output out_33,
  output out_34,
  output out_35,
  output out_36,
  output out_37,
  output out_38
);

  Decoder #(.select(5)) decoder_1 (
    .out0(out_7), .out1(out_8), .out2(out_9), .out3(out_10), .out4(out_11), .out5(out_12), .out6(out_13),
    .out7(out_14), .out8(out_15), .out9(out_16), .out10(out_17), .out11(out_18), .out12(out_19),
    .out13(out_20), .out14(out_21), .out15(out_22), .out16(out_23), .out17(out_24), .out18(out_25),
    .out19(out_26), .out20(out_27), .out21(out_28), .out22(out_29), .out23(out_30), .out24(out_31),
    .out25(out_32), .out26(out_33), .out27(out_34), .out28(out_35), .out29(out_36), .out30(out_37),
    .out31(out_38), .sel({in_2, in_3, in_4, in_5, in_6}), .en(in_1));
endmodule
