// Logisim project codificador.circ as structural Verilog: 1 circuit, main circuit main
module main (
  input  in_1,
  input  in_2,
  input  in_3,
  input  in_4,
  input  in_5,
  input  in_6,
  input  in_7,
  input  in_8,
  input  in_9,
  input  in_10,
  input  in_11,
  input  in_12,
  input  in_13,
  input  in_14,
  input  in_15,
  input  in_16,
  input  in_17,
  input  in_18,
  input  in_19,
  input  in_20,
  input  in_21,
  input  in_22,
  input  in_23,
  input  in_24,
  input  in_25,
  input  in_26,
  input  in_27,
  input  in_28,
  input  in_29,
  input  in_30,
  input  in_31,
  input  in_32,
  input  in_33,
  input  in_34,
  input  in_35,
  input  in_36,
  input  in_37,
  input  in_38,
  input  in_39,
  input  in_40,
  input  in_41,
  input  in_42,
  input  in_43,
  input  in_44,
  input  in_45,
  input  in_46,
  input  in_47,
  input  in_48,
  input  in_49,
  input  in_50,
  input  in_51,
  input  in_52,
  input  in_53,
  input  in_54,
  input  in_55,
  input  in_56,
  input  in_57,
  input  in_58,
  input  in_59,
  input  in_60,
  input  in_61,
  input  in_62,
  input  in_63,
  input  in_64,
  input  in_65,
  input  in_66,
  input  in_67,
  input  in_68,
  input  in_69,
  input  in_70,
  input  in_71,
  input  in_72,
  input  in_73,
  input  in_74,
  input  in_75,
  input  in_76,
  input  in_77,
  input  in_78,
  input  in_79,
  input  in_80,
  input  in_81,
  input  in_82,
  input  in_83,
  input  in_84,
  input  in_85,
  input  in_86,
  input  in_87,
  input  in_88,
  input  in_89,
  input  in_90,
  input  in_91,
  input  in_92,
  input  in_93,
  input  in_94,
  input  in_95,
  input  in_96,
  input  in_97,
  input  in_98,
  input  in_99,
  input  in_100,
  input  in_101,
  output out_102,
  output out_103,
  output [5:0] out_104,
  output [4:0] out_105,
  output out_106,
  output out_107,
  output out_108,
  output out_109
);

  wire and_1_out, or_1_out;
  wire [4:0] priority_encoder_2_out, priority_encoder_3_out;
  wire [5:0] bit_extender_1_out, bitselector_1_out, multiplexer_1_out;

  Priority_Encoder #(.select(5)) priority_encoder_1 (
    .in0(in_2), .in1(in_4), .in2(in_6), .in3(in_8), .in4(in_10), .in5(in_12), .in6(in_14), .in7(in_16),
    .in8(in_18), .in9(in_20), .in10(in_22), .in11(in_24), .in12(in_26), .in13(in_28), .in14(in_30),
    .in15(in_32), .in16(in_34), .in17(in_36), .in18(in_39), .in19(in_41), .in20(in_43), .in21(in_45),
    .in22(in_47), .in23(in_49), .in24(in_51), .in25(in_54), .in26(in_56), .in27(in_58), .in28(in_60),
    .in29(in_62), .in30(in_65), .in31(in_67), .out(out_105), .gs(out_107), .en_out(out_102), .en_in(in_53));
  Priority_Encoder #(.select(5)) priority_encoder_2 (
    .in0(in_1), .in1(in_3), .in2(in_5), .in3(in_7), .in4(in_9), .in5(in_11), .in6(in_13), .in7(in_15),
    .in8(in_17), .in9(in_19), .in10(in_21), .in11(in_23), .in12(in_25), .in13(in_27), .in14(in_29),
    .in15(in_31), .in16(in_33), .in17(in_35), .in18(in_37), .in19(in_40), .in20(in_42), .in21(in_44),
    .in22(in_46), .in23(in_48), .in24(in_50), .in25(in_52), .in26(in_55), .in27(in_57), .in28(in_59),
    .in29(in_61), .in30(in_63), .in31(in_66), .out(priority_encoder_2_out), .gs(out_106), .en_out(out_103),
    .en_in(in_64));
  Priority_Encoder #(.select(5)) priority_encoder_3 (
    .in0(in_68), .in1(in_69), .in2(in_70), .in3(in_71), .in4(in_73), .in5(in_74), .in6(in_75), .in7(in_76),
    .in8(in_77), .in9(in_78), .in10(in_79), .in11(in_80), .in12(in_81), .in13(in_82), .in14(in_83),
    .in15(in_84), .in16(in_85), .in17(in_86), .in18(in_87), .in19(in_88), .in20(in_89), .in21(in_90),
    .in22(in_91), .in23(in_92), .in24(in_93), .in25(in_95), .in26(in_96), .in27(in_97), .in28(in_98),
    .in29(in_99), .in30(in_100), .in31(in_101), .out(priority_encoder_3_out), .gs(out_109), .en_out(out_108),
    .en_in(in_94));
  BitSelector #(.group(6), .width(5)) bitselector_1 (.in(priority_encoder_2_out), .out(bitselector_1_out), .sel(in_38));
  and and_1 (and_1_out, out_106, out_109);
  assign bit_extender_1_out = {{1{1'b1}}, priority_encoder_3_out};  // Bit_Extender bit_extender_1
  or or_1 (or_1_out, and_1_out, out_109);
  Multiplexer #(.width(6)) multiplexer_1 (
    .in0(bitselector_1_out), .in1(bit_extender_1_out), .out(multiplexer_1_out), .sel(or_1_out));
  BitSelector #(.group(6), .width(6)) bitselector_2 (.in(multiplexer_1_out), .out(out_104), .sel(in_72));
endmodule
