// Logisim project mux_A_B.circ as structural Verilog: 2 circuits, main circuit main
module main (
  input  [63:0] in_1,
  input  [63:0] in_2,
  input  [63:0] in_3,
  input  [63:0] in_4,
  input  [63:0] in_5,
  input  [63:0] in_6,
  input  [63:0] in_7,
  input  [63:0] in_8,
  input  [63:0] in_9,
  input  [63:0] in_10,
  input  [63:0] in_11,
  input  [63:0] in_12,
  input  [63:0] in_13,
  input  [63:0] in_14,
  input  [63:0] in_15,
  input  [63:0] in_16,
  input  [63:0] in_17,
  input  [63:0] in_18,
  input  [63:0] in_19,
  input  [63:0] in_20,
  input  [63:0] in_21,
  input  [63:0] in_22,
  input  [63:0] in_23,
  input  [63:0] in_24,
  input  [63:0] in_25,
  input  [63:0] in_26,
  input  [63:0] in_27,
  input  [63:0] in_28,
  input  [63:0] in_29,
  input  [63:0] in_30,
  input  [63:0] in_31,
  input  [63:0] in_32,
  input  in_33,
  input  in_34,
  input  in_35,
  input  in_36,
  input  in_37,
  output [63:0] out_38
);

  Multiplexer #(.select(5), .width(64)) multiplexer_1 (
    .in0(in_1), .in1(in_2), .in2(in_3), .in3(in_4), .in4(in_5), .in5(in_6), .in6(in_7), .in7(in_8),
    .in8(in_9), .in9(in_10), .in10(in_11), .in11(in_12), .in12(in_13), .in13(in_14), .in14(in_15),
    .in15(in_16), .in16(in_17), .in17(in_18), .in18(in_19), .in19(in_20), .in20(in_21), .in21(in_22),
    .in22(in_23), .in23(in_24), .in24(in_25), .in25(in_26), .in26(in_27), .in27(in_28), .in28(in_29),
    .in29(in_30), .in30(in_31), .in31(in_32), .out(out_38), .sel({in_33, in_34, in_35, in_36, in_37}));
endmodule

module mux (
  input  [63:0] in_1,
  input  [63:0] in_2,
  input  [63:0] in_3,
  input  [63:0] in_4,
  input  [63:0] in_5,
  input  [63:0] in_6,
  input  [63:0] in_7,
  input  [63:0] in_8,
  input  [63:0] in_9,
  input  [63:0] in_10,
  input  [63:0] in_11,
  input  [63:0] in_12,
  input  [63:0] in_13,
  input  [63:0] in_14,
  input  [63:0] in_15,
  input  [63:0] in_16,
  input  [63:0] in_17,
  input  [63:0] in_18,
  input  [63:0] in_19,
  input  [63:0] in_20,
  input  [63:0] in_21,
  input  [63:0] in_22,
  input  [63:0] in_23,
  input  [63:0] in_24,
  input  [63:0] in_25,
  input  [63:0] in_26,
  input  [63:0] in_27,
  input  [63:0] in_28,
  input  [63:0] in_29,
  input  [63:0] in_30,
  input  [63:0] in_31,
  input  [63:0] in_32,
  input  in_33,
  input  in_34,
  input  in_35,
  input  in_36,
  input  in_37,
  output [63:0] out_38
);

  main main_1 (
    .in_1(in_1), .in_2(in_2), .in_3(in_3), .in_4(in_4), .in_5(in_5), .in_6(in_6), .in_7(in_7), .in_8(in_8),
    .in_9(in_9), .in_10(in_10), .in_11(in_11), .in_12(in_12), .in_13(in_13), .in_14(in_14), .in_15(in_15),
    .in_16(in_16), .in_17(in_17), .in_18(in_18), .in_19(in_19), .in_20(in_20), .in_21(in_21), .in_22(in_22),
    .in_23(in_23), .in_24(in_24), .in_25(in_25), .in_26(in_26), .in_27(in_27), .in_28(in_28), .in_29(in_29),
    .in_30(in_30), .in_31(in_31), .in_32(in_32), .in_33(in_33), .in_34(in_34), .in_35(in_35), .in_36(in_36),
    .in_37(in_37), .out_38(out_38));
endmodule
